// Logisim project nand2computer.circ as structural Verilog
module _101_Not (
  input  in,
  output out
);

  nand nand_1 (out, in, in);
endmodule

module _101_Not16 (
  input  [15:0] in_1,
  output [15:0] out_2
);

  _101_Not u_101_not_1 (.in(in_1[0]), .out(out_2[0]));
  _101_Not u_101_not_2 (.in(in_1[1]), .out(out_2[1]));
  _101_Not u_101_not_3 (.in(in_1[2]), .out(out_2[2]));
  _101_Not u_101_not_4 (.in(in_1[3]), .out(out_2[3]));
  _101_Not u_101_not_5 (.in(in_1[4]), .out(out_2[4]));
  _101_Not u_101_not_6 (.in(in_1[5]), .out(out_2[5]));
  _101_Not u_101_not_7 (.in(in_1[6]), .out(out_2[6]));
  _101_Not u_101_not_8 (.in(in_1[7]), .out(out_2[7]));
  _101_Not u_101_not_9 (.in(in_1[8]), .out(out_2[8]));
  _101_Not u_101_not_10 (.in(in_1[9]), .out(out_2[9]));
  _101_Not u_101_not_11 (.in(in_1[10]), .out(out_2[10]));
  _101_Not u_101_not_12 (.in(in_1[11]), .out(out_2[11]));
  _101_Not u_101_not_13 (.in(in_1[12]), .out(out_2[12]));
  _101_Not u_101_not_14 (.in(in_1[13]), .out(out_2[13]));
  _101_Not u_101_not_15 (.in(in_1[14]), .out(out_2[14]));
  _101_Not u_101_not_16 (.in(in_1[15]), .out(out_2[15]));
endmodule

module _102_And16 (
  input  in_1,
  output out_2
);

  wire clock_1_out;

  Clock #(.highDuration(1), .lowDuration(1)) clock_1 (.out(clock_1_out));
  D_Flip_Flop #(.trigger("rising"), .Pre_Clr_Positions("LEGACY"), .NegatePresetClear("false"), .enable("false"), .NewFFLayout("true")) d_ff_1 (
    .clk(clock_1_out), .D(in_1), .Q(out_2));  // open: Qn, preset, reset
endmodule
